# Fritzing sketch single_led (saved by Fritzing 0.9.3b)
breadboards: 1

parts:
  Part1 = Arduino Uno (Rev3)
  R1 = Resistor [tolerance=±5% resistance=330 package=THT]
  LED1 = LED - 3mm [color="Yellow (595nm)" package="3 mm [THT]"]

nets:
  N1: Part1.D10_PWM/SS, LED1.anode
  N2: Part1.GND, R1.Pin_0
  N3: R1.Pin_1, LED1.cathode

notes:
  V(led)
  V(res)
